// Logisim project tests.circ as structural Verilog: 13 circuits, main circuit Test_744511
module Test_7400 (
);

  wire and_1_out, clock_1_out, n7400_1_q1, n7400_1_q2, n7400_1_q3, n7400_1_q4, nand_1_out, xnor_1_out,
       xnor_2_out, xnor_3_out, xnor_4_out;
  wire [1:0] counter_1_q;

  Clock clock_1 (.out(clock_1_out));
  Counter #(.width(2), .max('h3)) counter_1 (
    .count(1'b1), .Q(counter_1_q), .clk(clock_1_out));  // open: load, D, carry, clr
  _7400 u_7400_1 (
    .A1(counter_1_q[0]), .B1(counter_1_q[1]), .A2(counter_1_q[0]), .B2(counter_1_q[1]), .A3(counter_1_q[0]),
    .B3(counter_1_q[1]), .A4(counter_1_q[0]), .B4(counter_1_q[1]), .Q1(n7400_1_q1), .Q2(n7400_1_q2),
    .Q3(n7400_1_q3), .Q4(n7400_1_q4));
  nand nand_1 (nand_1_out, counter_1_q[0], counter_1_q[1]);
  xnor xnor_1 (xnor_1_out, nand_1_out, n7400_1_q4);
  xnor xnor_2 (xnor_2_out, nand_1_out, n7400_1_q3);
  xnor xnor_3 (xnor_3_out, nand_1_out, n7400_1_q1);
  xnor xnor_4 (xnor_4_out, nand_1_out, n7400_1_q2);
  LED led_1 (.in(and_1_out));
  and and_1 (and_1_out, xnor_1_out, xnor_2_out, xnor_3_out, xnor_4_out);
endmodule

module Test_7402 (
);

  wire and_1_out, clock_1_out, n7402_1_q1, n7402_1_q2, n7402_1_q3, n7402_1_q4, nor_1_out, xnor_1_out,
       xnor_2_out, xnor_3_out, xnor_4_out;
  wire [1:0] counter_1_q;

  Clock clock_1 (.out(clock_1_out));
  Counter #(.width(2), .max('h3)) counter_1 (
    .count(1'b1), .Q(counter_1_q), .clk(clock_1_out));  // open: load, D, carry, clr
  _7402 u_7402_1 (
    .A1(counter_1_q[0]), .B1(counter_1_q[1]), .A2(counter_1_q[0]), .B2(counter_1_q[1]), .A3(counter_1_q[0]),
    .B3(counter_1_q[1]), .A4(counter_1_q[0]), .B4(counter_1_q[1]), .Q1(n7402_1_q1), .Q2(n7402_1_q2),
    .Q3(n7402_1_q3), .Q4(n7402_1_q4));
  nor nor_1 (nor_1_out, counter_1_q[0], counter_1_q[1]);
  xnor xnor_1 (xnor_1_out, nor_1_out, n7402_1_q4);
  xnor xnor_2 (xnor_2_out, nor_1_out, n7402_1_q3);
  xnor xnor_3 (xnor_3_out, nor_1_out, n7402_1_q1);
  xnor xnor_4 (xnor_4_out, nor_1_out, n7402_1_q2);
  LED led_1 (.in(and_1_out));
  and and_1 (and_1_out, xnor_1_out, xnor_2_out, xnor_3_out, xnor_4_out);
endmodule

module Test_7404 (
);

  wire and_1_out, clock_1_out, counter_1_q, n7404_1_q1, n7404_1_q2, n7404_1_q3, n7404_1_q4, n7404_1_q5,
       n7404_1_q6, not_1_out, xnor_1_out, xnor_2_out, xnor_3_out, xnor_4_out, xnor_5_out, xnor_6_out;

  Counter #(.width(1), .max('h1)) counter_1 (
    .count(1'b1), .Q(counter_1_q), .clk(clock_1_out));  // open: load, D, carry, clr
  Clock clock_1 (.out(clock_1_out));
  _7404 u_7404_1 (
    .A1(counter_1_q), .A2(counter_1_q), .A3(counter_1_q), .A4(counter_1_q), .A5(counter_1_q),
    .A6(counter_1_q), .Q1(n7404_1_q1), .Q2(n7404_1_q2), .Q3(n7404_1_q3), .Q4(n7404_1_q4), .Q5(n7404_1_q5),
    .Q6(n7404_1_q6));
  not not_1 (not_1_out, counter_1_q);
  xnor xnor_1 (xnor_1_out, not_1_out, n7404_1_q6);
  xnor xnor_2 (xnor_2_out, not_1_out, n7404_1_q5);
  xnor xnor_3 (xnor_3_out, not_1_out, n7404_1_q4);
  xnor xnor_4 (xnor_4_out, not_1_out, n7404_1_q1);
  xnor xnor_5 (xnor_5_out, not_1_out, n7404_1_q2);
  xnor xnor_6 (xnor_6_out, not_1_out, n7404_1_q3);
  LED led_1 (.in(and_1_out));
  and and_1 (and_1_out, xnor_1_out, xnor_2_out, xnor_3_out, xnor_4_out, xnor_5_out, xnor_6_out);
endmodule

module Test_7408 (
);

  wire and_1_out, and_2_out, clock_1_out, n7408_1_q1, n7408_1_q2, n7408_1_q3, n7408_1_q4, xnor_1_out,
       xnor_2_out, xnor_3_out, xnor_4_out;
  wire [1:0] counter_1_q;

  Clock clock_1 (.out(clock_1_out));
  Counter #(.width(2), .max('h3)) counter_1 (
    .count(1'b1), .Q(counter_1_q), .clk(clock_1_out));  // open: load, D, carry, clr
  _7408 u_7408_1 (
    .A1(counter_1_q[0]), .B1(counter_1_q[1]), .A2(counter_1_q[0]), .B2(counter_1_q[1]), .A3(counter_1_q[0]),
    .B3(counter_1_q[1]), .A4(counter_1_q[0]), .B4(counter_1_q[1]), .Q1(n7408_1_q1), .Q2(n7408_1_q2),
    .Q3(n7408_1_q3), .Q4(n7408_1_q4));
  and and_1 (and_1_out, counter_1_q[0], counter_1_q[1]);
  xnor xnor_1 (xnor_1_out, and_1_out, n7408_1_q3);
  xnor xnor_2 (xnor_2_out, and_1_out, n7408_1_q4);
  xnor xnor_3 (xnor_3_out, and_1_out, n7408_1_q1);
  xnor xnor_4 (xnor_4_out, and_1_out, n7408_1_q2);
  and and_2 (and_2_out, xnor_1_out, xnor_2_out, xnor_3_out, xnor_4_out);
  LED led_1 (.in(and_2_out));
endmodule

module Test_7410 (
);

  wire and_1_out, clock_1_out, n7410_1_q1, n7410_1_q2, n7410_1_q3, nand_1_out, xnor_1_out, xnor_2_out,
       xnor_3_out;
  wire [2:0] counter_1_q;

  Clock clock_1 (.out(clock_1_out));
  Counter #(.width(3), .max('h7)) counter_1 (
    .count(1'b1), .Q(counter_1_q), .clk(clock_1_out));  // open: load, D, carry, clr
  _7410 u_7410_1 (
    .A1(counter_1_q[0]), .B1(counter_1_q[1]), .C1(counter_1_q[2]), .A2(counter_1_q[0]), .B2(counter_1_q[1]),
    .C2(counter_1_q[2]), .A3(counter_1_q[0]), .B3(counter_1_q[1]), .C3(counter_1_q[2]), .Q1(n7410_1_q1),
    .Q2(n7410_1_q2), .Q3(n7410_1_q3));
  nand nand_1 (nand_1_out, counter_1_q[0], counter_1_q[1], counter_1_q[2]);
  xnor xnor_1 (xnor_1_out, nand_1_out, n7410_1_q1);
  xnor xnor_2 (xnor_2_out, nand_1_out, n7410_1_q3);
  xnor xnor_3 (xnor_3_out, nand_1_out, n7410_1_q2);
  LED led_1 (.in(and_1_out));
  and and_1 (and_1_out, xnor_1_out, xnor_2_out, xnor_3_out);
endmodule

module Test_7411 (
);

  wire and_1_out, and_2_out, clock_1_out, n7411_1_q1, n7411_1_q2, n7411_1_q3, xnor_1_out, xnor_2_out,
       xnor_3_out;
  wire [2:0] counter_1_q;

  Clock clock_1 (.out(clock_1_out));
  Counter #(.width(3), .max('h7)) counter_1 (
    .count(1'b1), .Q(counter_1_q), .clk(clock_1_out));  // open: load, D, carry, clr
  _7411 u_7411_1 (
    .A1(counter_1_q[0]), .B1(counter_1_q[1]), .C1(counter_1_q[2]), .A2(counter_1_q[0]), .B2(counter_1_q[1]),
    .C2(counter_1_q[2]), .A3(counter_1_q[0]), .B3(counter_1_q[1]), .C3(counter_1_q[2]), .Q1(n7411_1_q1),
    .Q2(n7411_1_q2), .Q3(n7411_1_q3));
  and and_1 (and_1_out, counter_1_q[0], counter_1_q[1], counter_1_q[2]);
  xnor xnor_1 (xnor_1_out, and_1_out, n7411_1_q1);
  xnor xnor_2 (xnor_2_out, and_1_out, n7411_1_q3);
  xnor xnor_3 (xnor_3_out, and_1_out, n7411_1_q2);
  LED led_1 (.in(and_2_out));
  and and_2 (and_2_out, xnor_1_out, xnor_2_out, xnor_3_out);
endmodule

module Test_7420 (
);

  wire and_1_out, clock_1_out, n7420_1_q1, n7420_1_q2, nand_1_out, xnor_1_out, xnor_2_out;
  wire [3:0] counter_1_q;

  Clock clock_1 (.out(clock_1_out));
  Counter #(.width(4), .max('hf)) counter_1 (
    .count(1'b1), .Q(counter_1_q), .clk(clock_1_out));  // open: load, D, carry, clr
  _7420 u_7420_1 (
    .A1(counter_1_q[0]), .B1(counter_1_q[1]), .C1(counter_1_q[2]), .D1(counter_1_q[3]), .A2(counter_1_q[0]),
    .B2(counter_1_q[1]), .C2(counter_1_q[2]), .D2(counter_1_q[3]), .Q1(n7420_1_q1), .Q2(n7420_1_q2));
  nand nand_1 (nand_1_out, counter_1_q[0], counter_1_q[1], counter_1_q[2], counter_1_q[3]);
  xnor xnor_1 (xnor_1_out, nand_1_out, n7420_1_q2);
  xnor xnor_2 (xnor_2_out, nand_1_out, n7420_1_q1);
  LED led_1 (.in(and_1_out));
  and and_1 (and_1_out, xnor_1_out, xnor_2_out);
endmodule

module Test_7421 (
);

  wire and_1_out, and_2_out, clock_1_out, n7421_1_q1, n7421_1_q2, xnor_1_out, xnor_2_out;
  wire [3:0] counter_1_q;

  Clock clock_1 (.out(clock_1_out));
  Counter #(.width(4), .max('hf)) counter_1 (
    .count(1'b1), .Q(counter_1_q), .clk(clock_1_out));  // open: load, D, carry, clr
  _7421 u_7421_1 (
    .A1(counter_1_q[0]), .B1(counter_1_q[1]), .C1(counter_1_q[2]), .D1(counter_1_q[3]), .A2(counter_1_q[0]),
    .B2(counter_1_q[1]), .C2(counter_1_q[2]), .D2(counter_1_q[3]), .Q1(n7421_1_q1), .Q2(n7421_1_q2));
  and and_1 (and_1_out, counter_1_q[0], counter_1_q[1], counter_1_q[2], counter_1_q[3]);
  xnor xnor_1 (xnor_1_out, and_1_out, n7421_1_q2);
  xnor xnor_2 (xnor_2_out, and_1_out, n7421_1_q1);
  and and_2 (and_2_out, xnor_1_out, xnor_2_out);
  LED led_1 (.in(and_2_out));
endmodule

module Test_7427 (
);

  wire and_1_out, clock_1_out, n7427_1_q1, n7427_1_q2, n7427_1_q3, nor_1_out, xnor_1_out, xnor_2_out,
       xnor_3_out;
  wire [2:0] counter_1_q;

  Clock clock_1 (.out(clock_1_out));
  Counter #(.width(3), .max('h7)) counter_1 (
    .count(1'b1), .Q(counter_1_q), .clk(clock_1_out));  // open: load, D, carry, clr
  _7427 u_7427_1 (
    .A1(counter_1_q[0]), .B1(counter_1_q[1]), .C1(counter_1_q[2]), .A2(counter_1_q[0]), .B2(counter_1_q[1]),
    .C2(counter_1_q[2]), .A3(counter_1_q[0]), .B3(counter_1_q[1]), .C3(counter_1_q[2]), .Q1(n7427_1_q1),
    .Q2(n7427_1_q2), .Q3(n7427_1_q3));
  nor nor_1 (nor_1_out, counter_1_q[0], counter_1_q[1], counter_1_q[2]);
  xnor xnor_1 (xnor_1_out, nor_1_out, n7427_1_q1);
  xnor xnor_2 (xnor_2_out, nor_1_out, n7427_1_q3);
  xnor xnor_3 (xnor_3_out, nor_1_out, n7427_1_q2);
  and and_1 (and_1_out, xnor_1_out, xnor_2_out, xnor_3_out);
  LED led_1 (.in(and_1_out));
endmodule

module Test_7432 (
);

  wire and_1_out, clock_1_out, n7432_1_q1, n7432_1_q2, n7432_1_q3, n7432_1_q4, or_1_out, xnor_1_out,
       xnor_2_out, xnor_3_out, xnor_4_out;
  wire [1:0] counter_1_q;

  Clock clock_1 (.out(clock_1_out));
  Counter #(.width(2), .max('h3)) counter_1 (
    .count(1'b1), .Q(counter_1_q), .clk(clock_1_out));  // open: load, D, carry, clr
  _7432 u_7432_1 (
    .A1(counter_1_q[0]), .B1(counter_1_q[1]), .A2(counter_1_q[0]), .B2(counter_1_q[1]), .A3(counter_1_q[0]),
    .B3(counter_1_q[1]), .A4(counter_1_q[0]), .B4(counter_1_q[1]), .Q1(n7432_1_q1), .Q2(n7432_1_q2),
    .Q3(n7432_1_q3), .Q4(n7432_1_q4));
  or or_1 (or_1_out, counter_1_q[0], counter_1_q[1]);
  xnor xnor_1 (xnor_1_out, or_1_out, n7432_1_q4);
  xnor xnor_2 (xnor_2_out, or_1_out, n7432_1_q3);
  xnor xnor_3 (xnor_3_out, or_1_out, n7432_1_q1);
  xnor xnor_4 (xnor_4_out, or_1_out, n7432_1_q2);
  LED led_1 (.in(and_1_out));
  and and_1 (and_1_out, xnor_1_out, xnor_2_out, xnor_3_out, xnor_4_out);
endmodule

module Test_4786 (
);

  wire and_1_out, clock_1_out, n7486_1_q1, n7486_1_q2, n7486_1_q3, n7486_1_q4, xnor_1_out, xnor_2_out,
       xnor_3_out, xnor_4_out, xor_1_out;
  wire [1:0] counter_1_q;

  Clock clock_1 (.out(clock_1_out));
  Counter #(.width(2), .max('h3)) counter_1 (
    .count(1'b1), .Q(counter_1_q), .clk(clock_1_out));  // open: load, D, carry, clr
  _7486 u_7486_1 (
    .A1(counter_1_q[0]), .B1(counter_1_q[1]), .A2(counter_1_q[0]), .B2(counter_1_q[1]), .A3(counter_1_q[0]),
    .B3(counter_1_q[1]), .A4(counter_1_q[0]), .B4(counter_1_q[1]), .Q1(n7486_1_q1), .Q2(n7486_1_q2),
    .Q3(n7486_1_q3), .Q4(n7486_1_q4));
  xor xor_1 (xor_1_out, counter_1_q[0], counter_1_q[1]);
  xnor xnor_1 (xnor_1_out, xor_1_out, n7486_1_q4);
  xnor xnor_2 (xnor_2_out, xor_1_out, n7486_1_q3);
  xnor xnor_3 (xnor_3_out, xor_1_out, n7486_1_q1);
  xnor xnor_4 (xnor_4_out, xor_1_out, n7486_1_q2);
  and and_1 (and_1_out, xnor_1_out, xnor_2_out, xnor_3_out, xnor_4_out);
  LED led_1 (.in(and_1_out));
endmodule

module Test_744075 (
);

  wire and_1_out, clock_1_out, n744075_1_q1, n744075_1_q2, n744075_1_q3, or_1_out, xnor_1_out, xnor_2_out,
       xnor_3_out;
  wire [2:0] counter_1_q;

  Clock clock_1 (.out(clock_1_out));
  Counter #(.width(3), .max('h7)) counter_1 (
    .count(1'b1), .Q(counter_1_q), .clk(clock_1_out));  // open: load, D, carry, clr
  _744075 u_744075_1 (
    .A1(counter_1_q[0]), .B1(counter_1_q[1]), .C1(counter_1_q[2]), .A2(counter_1_q[0]), .B2(counter_1_q[1]),
    .C2(counter_1_q[2]), .A3(counter_1_q[0]), .B3(counter_1_q[1]), .C3(counter_1_q[2]), .Q1(n744075_1_q1),
    .Q2(n744075_1_q2), .Q3(n744075_1_q3));
  or or_1 (or_1_out, counter_1_q[0], counter_1_q[1], counter_1_q[2]);
  xnor xnor_1 (xnor_1_out, or_1_out, n744075_1_q3);
  xnor xnor_2 (xnor_2_out, or_1_out, n744075_1_q2);
  xnor xnor_3 (xnor_3_out, or_1_out, n744075_1_q1);
  LED led_1 (.in(and_1_out));
  and and_1 (and_1_out, xnor_1_out, xnor_2_out, xnor_3_out);
endmodule

module Test_744511 (
  input  D3,
  input  D2,
  input  D1,
  input  D0,
  input  Load,
  input  Lamp_Test,
  input  Blank
);

  wire n744511_1_qa, n744511_1_qb, n744511_1_qc, n744511_1_qd, n744511_1_qe, n744511_1_qf, n744511_1_qg;

  _744511 u_744511_1 (
    .LT_(Lamp_Test), .A1(D0), .A2(D1), .A3(D2), .A4(D3), .LE(Load), .BL_(Blank), .Qa(n744511_1_qa),
    .Qb(n744511_1_qb), .Qc(n744511_1_qc), .Qd(n744511_1_qd), .Qe(n744511_1_qe), .Qf(n744511_1_qf),
    .Qg(n744511_1_qg));
  _7_Segment_Display u_7_segment_display_1 (
    .g(n744511_1_qg), .f(n744511_1_qf), .a(n744511_1_qa), .b(n744511_1_qb), .e(n744511_1_qe),
    .d(n744511_1_qd), .c(n744511_1_qc));  // open: dp
endmodule
